# Fritzing sketch schematic (saved by Fritzing 0.9.3b)
breadboards: 1

parts:
  R1 = Resistor [tolerance=±5% resistance=10k package=THT]
  R2 = Photocell (LDR) [package=THT]
  Raspberry_Pi_1 = Raspberry Pi 3 [part_number=RPI-3-V1.2]  # not connected
  Part1 = Arduino Leonardo (Rev3b)

nets:
  N1: R1.Pin_0, Part1.GND
  N2: R1.Pin_1, R2.pin_0, Part1.A0
  N3: R2.pin_1, Part1.5V

notes:
  Arduino and Raspberry Pi are connected with a USB Cable
